# Fritzing sketch circuit (saved by Fritzing 0.9.6b)
breadboards: 1

parts:
  Componente1 = Arduino Uno (Rev3)
  SERVO1 = Tower Pro SG90 servo [part_number=101246]
  S1 = Pushbutton [package="[THT]"]
  S2 = Pushbutton [package="[THT]"]
  S3 = Pushbutton [package="[THT]"]
  S4 = Pushbutton [package="[THT]"]
  R1 = Resistor [tolerance=±5% power=0.25 resistance=10k package=THT]
  R2 = Resistor [tolerance=±5% power=0.25 resistance=10k package=THT]
  R3 = Resistor [tolerance=±5% power=0.25 resistance=10k package=THT]
  R4 = Resistor [tolerance=±5% power=0.25 resistance=10k package=THT]
  SM1 = 28BYJ-48 Stepper Motor [part_number=28BYJ-48]
  Driver1 = 28BYJ-48 Driver Module [part_number=ULN2003 package=THT]
  RE1 = KY-040 Rotary encoder [package=THT]
  J1 = Piezo Speaker
  R5 = Resistor [tolerance=±5% power=0.25 resistance=1M package=THT]
  R6 = Resistor [tolerance=±5% power=0.25 resistance=220 package=THT]
  M1 = DC Motor
  M2 = DC Motor
  M3 = DC Motor
  M4 = DC Motor
  LED1 = LED - 5mm [color="Green (555nm)" current=0.030 package="5 mm [THT]"]
  Componente3 = Adafruit TCS34725 RGB Color Sensor [part_number="Adafruit #1334"]
  Display2 = LCD screen 16x2 IIC [part_number=101290]
  KY-2 = Keyes Relay [package=THT]
  Mod2 = generic-ac-power-supply [package=THT]

nets:
  N1: Componente1.A0, KY-2.signal
  N2: Componente1.A1, J1.pin2, R5.Pin_0
  N3: Componente1.A4/SDA, Componente3.SDA, Display2.SDA
  N4: Componente1.A5/SCL, Componente3.SCL, Display2.SCL
  N5: Componente1.D8, Driver1.IN1
  N6: Componente1.D9_PWM, Driver1.IN2
  N7: Componente1.D10_PWM/SS, Driver1.IN3
  N8: Componente1.D11_PWM/MOSI, Driver1.IN4
  N9: Componente1.D12/MISO, SERVO1.Signal
  N10: Componente1.D13/SCK, LED1.anode
  N11: Componente1.D2, S4.Pin_3, S4.Pin_4, R4.Pin_0
  N12: Componente1.D3_PWM, S3.Pin_3, S3.Pin_4, R3.Pin_0
  N13: Componente1.D4, S2.Pin_3, S2.Pin_4, R2.Pin_0
  N14: Componente1.D5_PWM, S1.Pin_3, S1.Pin_4, R1.Pin_0
  N15: Componente1.D6_PWM, RE1.CLK
  N16: Componente1.D7, RE1.DT
  VCC: Componente1.5V, SERVO1.+5V, S1.Pin_1, S1.Pin_2, S2.Pin_1, S2.Pin_2, S3.Pin_1, S3.Pin_2, S4.Pin_1, S4.Pin_2, RE1.Vcc, Componente3.VIN, Display2.VCC, KY-2.power
  GND: Componente1.GND, SERVO1.GND, R1.Pin_1, R2.Pin_1, R3.Pin_1, R4.Pin_1, RE1.GND, J1.pin1, R5.Pin_1, R6.Pin_1, Componente3.GND, Display2.GND, KY-2.ground
  N17: SM1.blue-pin, Driver1.blue-pin
  N18: SM1.pink-pin, Driver1.pink-pin
  N19: SM1.yellow-pin, Driver1.yellow-pin
  N20: SM1.orange-pin, Driver1.orange-pin
  N21: SM1.red-pin, Driver1.red-pin
  N22: R6.Pin_0, LED1.cathode
  N23: M1.pin_1, Mod2.pin3#2
  N24: M1.pin_2, M2.pin_1
  N25: M2.pin_2, M3.pin_1
  N26: M3.pin_2, M4.pin_1
  N27: M4.pin_2, KY-2.NO
  N28: Componente3.INT, Componente3.LED_EN

custom parts:
  Tower Pro SG90 servo: Original file by John De Cristofaro http://www.adafruit.com/products/1449 Adafruit Feedback Servo (Small) Edited by: e-radionica.com 28/9/2015
  28BYJ-48 Stepper Motor: Unipolar Stepper Motor 28BYJ-48 Top coil - pink & orange Bottom coil - blue & yellow Common rail - red Connector pins: blue - pink - yellow - orange - red
  28BYJ-48 Driver Module: ULN2003 Driver Module for the 28BYJ-48 Unipolar Stepper Motor LED A - Blue wire - Bottom coil left LED B - Pink wire - Top coil left LED C - Yellow wire - Bottom coil right LED D - Orange wire - Top coil right Common rail - red Connector pins: blue - pink - yellow - orange - red Control pins - IN1 to IN4 Power pins - GND & Vmotor (5-12V) On/Off jumper (if removed, power to motor is cut).
  KY-040 Rotary encoder: KY-040 Rotary Encoder with switch on breakout borad from AZ Delivery
  Adafruit TCS34725 RGB Color Sensor: Your electronics can now see in dazzling color with this lovely color light sensor. We found the best color sensor on the market, the TCS34725, which has RGB and Clear light sensing elements. An IR blocking filter, integrated on-chip and localized to the color sensing photodiodes, minimizes the IR spectral component of the incoming light and allows color measurements to be made accurately. The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
  LCD screen 16x2 IIC: LCD screen with HD44780 controller enables showing text, symbols, value or anything else that comes from Croduino/Arduino. It is capable of showing 16 symbols in two lines and therefore can be used in many projects that need to send clearly visible and legible output information.. • Color of symbols: White • Backlight: Blue • Dimensions: 80 x 36 x 12 mm • Screen dimensions: 64.5 x 16 mm •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
  Keyes Relay: The Keyes 5V relay module is suitable for SCM development, home appliance control. It uses a 5V~12V TIL control signal which can control DC / AC signal.
  generic-ac-power-supply: Generic ac power supply module. Use as is, or customize the svgs to fit your particular device (as they are all different.) Provides AC input and single DC output. PCB is generic and will need modifications if you intend to do a pcb mount.
